// Logisim project ControlUnit.circ as structural Verilog: 3 circuits, main circuit ControlUnit
module ControlUnit (
  input  [5:0] in_1,
  input  [5:0] in_2,
  output out_3,
  output out_4,
  output out_5,
  output out_6,
  output out_7,
  output out_8,
  output out_9,
  output [2:0] out_10
);

  wire [1:0] main_decoder_1_aluop_1_0;

  Main_Decoder main_decoder_1 (
    .Opcode_5_0(in_1), .MemtoReg(out_4), .MemWrite(out_5), .Branch(out_6), .ALUSrc(out_7), .RegDst(out_8),
    .RegWrite(out_9), .Jump(out_3), .ALUOp_1_0(main_decoder_1_aluop_1_0));
  ALU_Decoder alu_decoder_1 (.ALUOp_1_0(main_decoder_1_aluop_1_0), .Funct_5_0(in_2), .ALUCtrl_2_0(out_10));
endmodule

module ALU_Decoder (
  input  [1:0] ALUOp_1_0,
  input  [5:0] Funct_5_0,
  output [2:0] ALUCtrl_2_0
);

  wire and_1_out, and_2_out, and_3_out;

  and and_1 (and_1_out, ALUOp_1_0[1], Funct_5_0[1]);
  and and_2 (and_2_out, ALUOp_1_0[1], Funct_5_0[0]);
  and and_3 (and_3_out, ALUOp_1_0[1], Funct_5_0[3]);
  or or_1 (ALUCtrl_2_0[2], ALUOp_1_0[0], and_1_out);
  or or_2 (ALUCtrl_2_0[1], ~ALUOp_1_0[1], ~Funct_5_0[2]);  // OR_Gate
  or or_3 (ALUCtrl_2_0[0], and_2_out, and_3_out);
endmodule

module Main_Decoder (
  input  [5:0] Opcode_5_0,
  output MemtoReg,
  output MemWrite,
  output Branch,
  output ALUSrc,
  output RegDst,
  output RegWrite,
  output Jump,
  output [1:0] ALUOp_1_0
);

  wire and_3_out, and_4_out;

  and and_1 (MemWrite, Opcode_5_0[5], Opcode_5_0[3]);
  and and_2 (RegDst, ~Opcode_5_0[3], ~Opcode_5_0[1]);  // AND_Gate
  and and_3 (and_3_out, ~Opcode_5_0[2], ~Opcode_5_0[1]);  // AND_Gate
  and and_4 (and_4_out, Opcode_5_0[5], ~Opcode_5_0[3]);  // AND_Gate
  and and_5 (Jump, Opcode_5_0[1], ~Opcode_5_0[0]);  // AND_Gate
  and and_6 (ALUOp_1_0[1], ~Opcode_5_0[3], ~Opcode_5_0[2], ~Opcode_5_0[1]);  // AND_Gate
  or or_1 (ALUSrc, Opcode_5_0[1], Opcode_5_0[3]);
  or or_2 (RegWrite, and_3_out, and_4_out);

  assign ALUOp_1_0[0] = Opcode_5_0[2];
  assign Branch = Opcode_5_0[2];
  assign MemtoReg = Opcode_5_0[5];
endmodule
