// Logisim project MIPS.circ as structural Verilog: 2 circuits, main circuit main
module main (
  input  CLR
);

  wire alu_1_zero, and_1_out, and_2_out, BranchD, button_1_out, CLK, comparator_1_eq, controlunit_1_out_3,
       controlunit_1_out_4, controlunit_1_out_5, controlunit_1_out_7, controlunit_1_out_8,
       controlunit_1_out_9, d_ff_1_q, delay_1_out_2, hazard_unit_1_p5, hazard_unit_1_p6, hazard_unit_1_p8,
       hazard_unit_1_p9, hazard_unit_1_p11, not_1_out, not_2_out, reg_stage2_1_alusrce, reg_stage2_1_errore,
       reg_stage2_1_memwritee, reg_stage2_1_regdste, reg_stage3_1_p12, reg_stage4_1_memtoregw, undriven,
       undriven_2, undriven_3, undriven_4, undriven_5, undriven_6;
  wire [1:0] hazard_unit_1_p2, hazard_unit_1_p3;
  wire [3:0] adder_1_out_2, controlunit_1_out_10, reg_stage2_1_aluctrle;
  wire [4:0] hazard_unit_1_p1, hazard_unit_1_p4, hazard_unit_1_p7, hazard_unit_1_p10, reg_stage1_1_instrd_2,
       reg_stage2_1_rde, reg_stage2_1_rse;
  wire [25:0] reg_stage1_1_instrd;
  wire [27:0] adder_1_out, bit_extender_1_out, shifter_1_out;
  wire [31:0] adder_2_out, alu_1_alu_result, bit_extender_2_out, datamem_1_rd, instmem_1_out_2,
       multiplexer_1_out, multiplexer_2_out, multiplexer_3_out, multiplexer_4_out, multiplexer_6_out,
       multiplexer_7_out, multiplexer_8_out, multiplexer_9_out, PC_q, reg_stage1_1_pcplus4d,
       reg_stage2_1_signimme, reg_stage2_1_srcae, reg_stage2_1_srcbe, reg_stage3_1_p15, reg_stage3_1_p16,
       reg_stage4_1_aluoutw, reg_stage4_1_readdataw, regfile32_1_rd1, regfile32_1_rd2, shifter_2_out;
  wire [31:26] reg_stage1_1_instrd_3;

  Clock clock_1 (.out(CLK));
  Multiplexer #(.width(32)) multiplexer_1 (
    .in0({adder_1_out_2, adder_1_out}), .in1(adder_2_out), .out(multiplexer_1_out), .sel(and_2_out));  // open: en
  Multiplexer #(.width(32)) multiplexer_2 (
    .in0(multiplexer_1_out), .in1({adder_1_out_2, shifter_1_out}), .out(multiplexer_2_out),
    .sel(controlunit_1_out_3));  // open: en
  not not_1 (not_1_out, undriven);
  Button button_1 (.out(button_1_out));
  assign bit_extender_1_out = {{2{reg_stage1_1_instrd[25]}}, {reg_stage1_1_instrd[25:21], reg_stage1_1_instrd_2, reg_stage1_1_instrd[15:0]}};  // Bit_Extender bit_extender_1
  Register #(.width(32)) PC (.D(multiplexer_2_out), .en(not_1_out), .Q(PC_q), .clk(CLK), .clr(button_1_out));
  Shifter #(.width(28)) shifter_1 (.in(bit_extender_1_out), .\dist (5'b00010), .out(shifter_1_out));
  InstMem instmem_1 (.A(PC_q), .out_2(instmem_1_out_2));
  Adder #(.width(32)) adder_1 (.a(PC_q), .b(32'h4), .out({adder_1_out_2, adder_1_out}));  // open: cin, cout
  D_Flip_Flop #(.trigger("falling")) d_ff_1 (.clk(CLK), .D(and_2_out), .Q(d_ff_1_q));  // open: Qn, preset, en, reset
  not not_2 (not_2_out, undriven_2);
  and and_1 (and_1_out, CLK, d_ff_1_q);
  Reg_Stage1 reg_stage1_1 (
    .CLR(and_1_out), .EN(not_2_out), .CLK(CLK), .InstrF(instmem_1_out_2),
    .PCPlus4F({adder_1_out_2, adder_1_out}),
    .InstrD({reg_stage1_1_instrd_3, reg_stage1_1_instrd[25:21], reg_stage1_1_instrd_2, reg_stage1_1_instrd[15:0]}),
    .PCPlus4D(reg_stage1_1_pcplus4d));
  ControlUnit controlunit_1 (
    .out_3(controlunit_1_out_3), .in_1(reg_stage1_1_instrd_3), .in_2(reg_stage1_1_instrd[5:0]),
    .out_4(controlunit_1_out_4), .out_5(controlunit_1_out_5), .out_6(BranchD), .out_7(controlunit_1_out_7),
    .out_8(controlunit_1_out_8), .out_9(controlunit_1_out_9), .out_10(controlunit_1_out_10));
  Delay delay_1 (.in_1(CLK), .out_2(delay_1_out_2));
  RegFile32 regfile32_1 (
    .AD1(reg_stage1_1_instrd[25:21]), .AD2(reg_stage1_1_instrd_2), .CLK(delay_1_out_2),
    .WE(hazard_unit_1_p11), .AD3(hazard_unit_1_p10), .WD3(multiplexer_9_out), .RD1(regfile32_1_rd1),
    .RD2(regfile32_1_rd2));
  assign bit_extender_2_out = {{16{reg_stage1_1_instrd[15]}}, reg_stage1_1_instrd[15:0]};  // Bit_Extender bit_extender_2
  Multiplexer #(.width(32)) multiplexer_3 (
    .in0(regfile32_1_rd1), .in1(reg_stage3_1_p15), .out(multiplexer_3_out), .sel(undriven_4));  // open: en
  Multiplexer #(.width(32)) multiplexer_4 (
    .in0(regfile32_1_rd2), .in1(reg_stage3_1_p15), .out(multiplexer_4_out), .sel(undriven_5));  // open: en
  Shifter #(.width(32)) shifter_2 (.in(bit_extender_2_out), .\dist (5'b00010), .out(shifter_2_out));
  Comparator #(.width(32)) comparator_1 (
    .a(multiplexer_3_out), .b(multiplexer_4_out), .eq(comparator_1_eq));  // open: gt, lt
  Adder #(.width(32)) adder_2 (.a(shifter_2_out), .b(reg_stage1_1_pcplus4d), .out(adder_2_out));  // open: cin, cout
  // Hazard_Unit hazard_unit_1: pin names not known; wires that end beside it: hazard_unit_1_p1, hazard_unit_1_p2, hazard_unit_1_p3, hazard_unit_1_p4, hazard_unit_1_p5, hazard_unit_1_p6, hazard_unit_1_p7, hazard_unit_1_p8, hazard_unit_1_p9, hazard_unit_1_p10, hazard_unit_1_p11
  and and_2 (and_2_out, comparator_1_eq, undriven_3, BranchD);
  Reg_Stage2 reg_stage2_1 (
    .CLK(CLK), .CLR(undriven_6), .EN(1'b1), .ErrorD(undriven_3), .MemtoRegD(controlunit_1_out_4),
    .MemWriteD(controlunit_1_out_5), .BranchD(BranchD), .ALUSrcD(controlunit_1_out_7),
    .RegDstD(controlunit_1_out_8), .RegWriteD(controlunit_1_out_9), .ALUCtrlD(controlunit_1_out_10),
    .SrcAD(regfile32_1_rd1), .SrcBD(regfile32_1_rd2), .RtD(reg_stage1_1_instrd_2),
    .RdD(reg_stage1_1_instrd[15:11]), .SignImmD(bit_extender_2_out), .ErrorE(reg_stage2_1_errore),
    .MemtoRegE(hazard_unit_1_p5), .MemWriteE(reg_stage2_1_memwritee), .ALUSrcE(reg_stage2_1_alusrce),
    .RegDstE(reg_stage2_1_regdste), .RegWriteE(hazard_unit_1_p6), .ALUCtrlE(reg_stage2_1_aluctrle),
    .SrcAE(reg_stage2_1_srcae), .SrcBE(reg_stage2_1_srcbe), .RtE(hazard_unit_1_p1), .RdE(reg_stage2_1_rde),
    .SignImmE(reg_stage2_1_signimme), .RsD(reg_stage1_1_instrd[25:21]), .RsE(reg_stage2_1_rse));  // open: PCPlus4D, BranchE, PCPlus4E
  Multiplexer #(.width(5)) multiplexer_5 (
    .in0(hazard_unit_1_p1), .in1(reg_stage2_1_rde), .out(hazard_unit_1_p4), .sel(reg_stage2_1_regdste));  // open: en
  Multiplexer #(.width(32)) multiplexer_6 (
    .in0(reg_stage2_1_srcbe), .in1(reg_stage2_1_signimme), .out(multiplexer_6_out), .sel(reg_stage2_1_alusrce));  // open: en
  Multiplexer #(.select(2), .width(32)) multiplexer_7 (
    .in0(reg_stage2_1_srcae), .in1(reg_stage3_1_p15), .in2(multiplexer_9_out), .out(multiplexer_7_out),
    .sel(hazard_unit_1_p2));  // open: in3, en
  Multiplexer #(.select(2), .width(32)) multiplexer_8 (
    .in0(multiplexer_6_out), .in1(reg_stage3_1_p15), .in2(multiplexer_9_out), .out(multiplexer_8_out),
    .sel(hazard_unit_1_p3));  // open: in3, en
  ALU alu_1 (
    .SrcA(multiplexer_7_out), .SrcB(multiplexer_8_out), .ALU_Control(reg_stage2_1_aluctrle),
    .Zero(alu_1_zero), .ALU_Result(alu_1_alu_result));
  // Reg_Stage3 reg_stage3_1: pin names not known; wires that end beside it: reg_stage2_1_errore, hazard_unit_1_p5, reg_stage2_1_memwritee, hazard_unit_1_p6, alu_1_zero, alu_1_alu_result, reg_stage2_1_srcbe, hazard_unit_1_p4, 1'b1, CLK, CLR, reg_stage3_1_p12, hazard_unit_1_p8, hazard_unit_1_p9, reg_stage3_1_p15, reg_stage3_1_p16, hazard_unit_1_p7
  DataMem datamem_1 (.CLK(CLK), .WE(hazard_unit_1_p8), .WD(reg_stage3_1_p16), .A(reg_stage3_1_p15), .RD(datamem_1_rd));
  Reg_Stage4 reg_stage4_1 (
    .CLR(CLR), .EN(1'b1), .CLK(CLK), .RegWriteM(hazard_unit_1_p9), .MemtoRegM(reg_stage3_1_p12),
    .ALUOutM(reg_stage3_1_p15), .ReadDataM(datamem_1_rd), .WriteRegM(hazard_unit_1_p7),
    .RegWriteW(hazard_unit_1_p11), .MemtoRegW(reg_stage4_1_memtoregw), .ALUOutW(reg_stage4_1_aluoutw),
    .ReadDataW(reg_stage4_1_readdataw), .WriteRegW(hazard_unit_1_p10));
  Multiplexer #(.width(32)) multiplexer_9 (
    .in0(reg_stage4_1_aluoutw), .in1(reg_stage4_1_readdataw), .out(multiplexer_9_out),
    .sel(reg_stage4_1_memtoregw));  // open: en
endmodule

module Delay (
  input  in_1,
  output out_2
);

  wire buffer_1_out, buffer_2_out, buffer_3_out, buffer_4_out, buffer_5_out, buffer_6_out, buffer_7_out,
       buffer_8_out, buffer_9_out, buffer_10_out, buffer_11_out, buffer_12_out, buffer_13_out, buffer_14_out,
       buffer_15_out, buffer_16_out, buffer_17_out, buffer_18_out, buffer_19_out, buffer_20_out,
       buffer_21_out, buffer_22_out, buffer_23_out, buffer_24_out, buffer_25_out, buffer_26_out,
       buffer_27_out, buffer_28_out, buffer_29_out, buffer_30_out, buffer_31_out;

  buf buffer_1 (buffer_1_out, buffer_2_out);
  buf buffer_2 (buffer_2_out, in_1);
  buf buffer_3 (buffer_3_out, buffer_1_out);
  buf buffer_4 (buffer_4_out, buffer_3_out);
  buf buffer_5 (buffer_5_out, buffer_6_out);
  buf buffer_6 (buffer_6_out, buffer_4_out);
  buf buffer_7 (buffer_7_out, buffer_8_out);
  buf buffer_8 (buffer_8_out, buffer_10_out);
  buf buffer_9 (buffer_9_out, buffer_5_out);
  buf buffer_10 (buffer_10_out, buffer_9_out);
  buf buffer_11 (buffer_11_out, buffer_7_out);
  buf buffer_12 (buffer_12_out, buffer_13_out);
  buf buffer_13 (buffer_13_out, buffer_14_out);
  buf buffer_14 (buffer_14_out, buffer_11_out);
  buf buffer_15 (buffer_15_out, buffer_18_out);
  buf buffer_16 (buffer_16_out, buffer_12_out);
  buf buffer_17 (buffer_17_out, buffer_15_out);
  buf buffer_18 (buffer_18_out, buffer_16_out);
  buf buffer_19 (buffer_19_out, buffer_20_out);
  buf buffer_20 (buffer_20_out, buffer_17_out);
  buf buffer_21 (buffer_21_out, buffer_22_out);
  buf buffer_22 (buffer_22_out, buffer_19_out);
  buf buffer_23 (buffer_23_out, buffer_25_out);
  buf buffer_24 (buffer_24_out, buffer_21_out);
  buf buffer_25 (buffer_25_out, buffer_24_out);
  buf buffer_26 (buffer_26_out, buffer_23_out);
  buf buffer_27 (buffer_27_out, buffer_26_out);
  buf buffer_28 (buffer_28_out, buffer_29_out);
  buf buffer_29 (buffer_29_out, buffer_30_out);
  buf buffer_30 (buffer_30_out, buffer_27_out);
  buf buffer_31 (buffer_31_out, buffer_28_out);
  buf buffer_32 (out_2, buffer_31_out);
endmodule
